// Logisim project SingleCycleProcessor.circ as structural Verilog: 4 circuits, main circuit RegFile
module RegFile (
  input  [2:0] S1,
  input  [2:0] S2,
  input  [31:0] Rx,
  input  [2:0] RegDest,
  input  WE,
  input  CLK,
  output [31:0] Reg1,
  output [31:0] Reg2
);

  wire and_1_out, and_2_out, and_3_out, and_4_out, and_5_out, and_6_out, and_7_out, decoder_1_out0,
       decoder_2_out0, decoder_2_out1, decoder_2_out2, decoder_2_out3, decoder_2_out4, decoder_2_out5,
       decoder_2_out6, decoder_2_out7, decoder_3_out0, decoder_3_out1, decoder_3_out2, decoder_3_out3,
       decoder_3_out4, decoder_3_out5, decoder_3_out6, decoder_3_out7, r1, r2, r3, r4, r5, r6, r7;
  wire [31:0] register_1_q, register_2_q, register_3_q, register_4_q, register_5_q, register_6_q,
       register_7_q;

  Decoder #(.select(3), .enable("false")) decoder_1 (
    .out0(decoder_1_out0), .out1(r1), .out2(r2), .out3(r3), .out4(r4), .out5(r5), .out6(r6), .out7(r7),
    .sel(RegDest));
  and and_1 (and_1_out, r1, WE);
  and and_2 (and_2_out, r2, WE);
  and and_3 (and_3_out, r3, WE);
  and and_4 (and_4_out, r4, WE);
  and and_5 (and_5_out, r5, WE);
  and and_6 (and_6_out, r6, WE);
  and and_7 (and_7_out, r7, WE);
  Decoder #(.select(3), .enable("false")) decoder_2 (
    .out0(decoder_2_out0), .out1(decoder_2_out1), .out2(decoder_2_out2), .out3(decoder_2_out3),
    .out4(decoder_2_out4), .out5(decoder_2_out5), .out6(decoder_2_out6), .out7(decoder_2_out7), .sel(S1));
  assign Reg1 = decoder_2_out0 ? {32{1'b0}} : 32'bz;  // Controlled_Buffer controlled_buffer_1
  assign Reg1 = decoder_2_out1 ? register_1_q : 32'bz;  // Controlled_Buffer controlled_buffer_2
  Register #(.width(32)) register_1 (.D(Rx), .en(and_1_out), .Q(register_1_q), .clk(CLK));  // open: clr
  assign Reg1 = decoder_2_out2 ? register_2_q : 32'bz;  // Controlled_Buffer controlled_buffer_3
  Register #(.width(32)) register_2 (.D(Rx), .en(and_2_out), .Q(register_2_q), .clk(CLK));  // open: clr
  assign Reg1 = decoder_2_out3 ? register_3_q : 32'bz;  // Controlled_Buffer controlled_buffer_4
  Register #(.width(32)) register_3 (.D(Rx), .en(and_3_out), .Q(register_3_q), .clk(CLK));  // open: clr
  assign Reg1 = decoder_2_out4 ? register_4_q : 32'bz;  // Controlled_Buffer controlled_buffer_5
  Register #(.width(32)) register_4 (.D(Rx), .en(and_4_out), .Q(register_4_q), .clk(CLK));  // open: clr
  assign Reg1 = decoder_2_out5 ? register_5_q : 32'bz;  // Controlled_Buffer controlled_buffer_6
  Register #(.width(32)) register_5 (.D(Rx), .en(and_5_out), .Q(register_5_q), .clk(CLK));  // open: clr
  assign Reg1 = decoder_2_out6 ? register_6_q : 32'bz;  // Controlled_Buffer controlled_buffer_7
  Register #(.width(32)) register_6 (.D(Rx), .en(and_6_out), .Q(register_6_q), .clk(CLK));  // open: clr
  assign Reg1 = decoder_2_out7 ? register_7_q : 32'bz;  // Controlled_Buffer controlled_buffer_8
  Register #(.width(32)) register_7 (.D(Rx), .en(and_7_out), .Q(register_7_q), .clk(CLK));  // open: clr
  assign Reg2 = decoder_3_out0 ? {32{1'b0}} : 32'bz;  // Controlled_Buffer controlled_buffer_9
  assign Reg2 = decoder_3_out1 ? register_1_q : 32'bz;  // Controlled_Buffer controlled_buffer_10
  assign Reg2 = decoder_3_out2 ? register_2_q : 32'bz;  // Controlled_Buffer controlled_buffer_11
  assign Reg2 = decoder_3_out3 ? register_3_q : 32'bz;  // Controlled_Buffer controlled_buffer_12
  assign Reg2 = decoder_3_out4 ? register_4_q : 32'bz;  // Controlled_Buffer controlled_buffer_13
  assign Reg2 = decoder_3_out5 ? register_5_q : 32'bz;  // Controlled_Buffer controlled_buffer_14
  assign Reg2 = decoder_3_out6 ? register_6_q : 32'bz;  // Controlled_Buffer controlled_buffer_15
  assign Reg2 = decoder_3_out7 ? register_7_q : 32'bz;  // Controlled_Buffer controlled_buffer_16
  Decoder #(.select(3), .enable("false")) decoder_3 (
    .out0(decoder_3_out0), .out1(decoder_3_out1), .out2(decoder_3_out2), .out3(decoder_3_out3),
    .out4(decoder_3_out4), .out5(decoder_3_out5), .out6(decoder_3_out6), .out7(decoder_3_out7), .sel(S2));
  // Probe on register_1_q
  // Probe on register_2_q
  // Probe on register_3_q
  // Probe on register_4_q
  // Probe on register_5_q
  // Probe on register_6_q
  // Probe on register_7_q
  // also tied to GND on the sheet: decoder_1_out0
endmodule

module ALU (
  input  [31:0] R1,
  input  [31:0] R2,
  input  [3:0] opCode,
  output [31:0] Result,
  output c_flag,
  output zero_flag,
  output N_flag
);

  wire adder_1_cout, comparator_1_eq, comparator_1_lt, not_2_out, subtractor_1_bout;
  wire [31:0] adder_1_out, and_1_out, and_2_out, bit_extender_1_out, bit_extender_2_out, not_1_out, or_1_out,
       shifter_1_out, shifter_2_out, shifter_3_out, shifter_4_out, subtractor_1_out, xor_1_out;

  assign not_1_out = ~R1;  // NOT_Gate not_1, 32 bits wide
  assign xor_1_out = R1 ^ R2;  // XOR_Gate xor_1, 32 bits wide
  assign and_1_out = R1 & R2;  // AND_Gate and_1, 32 bits wide
  assign or_1_out = R1 | R2;  // OR_Gate or_1, 32 bits wide
  assign and_2_out = not_1_out & R2;  // AND_Gate and_2, 32 bits wide
  Adder #(.width(32)) adder_1 (.a(R1), .b(R2), .out(adder_1_out), .cin(1'b0), .cout(adder_1_cout));
  Comparator #(.width(32)) comparator_1 (.a(R1), .b(R2), .eq(comparator_1_eq), .lt(comparator_1_lt));  // open: gt
  Subtractor #(.width(32)) subtractor_1 (.a(R2), .b(R1), .out(subtractor_1_out), .bin(1'b0), .bout(subtractor_1_bout));
  Shifter #(.width(32), .shift("ar")) shifter_1 (.in(R1), .\dist (R2[4:0]), .out(shifter_1_out));
  Shifter #(.width(32), .shift("lr")) shifter_2 (.in(R1), .\dist (R2[4:0]), .out(shifter_2_out));
  Shifter #(.width(32)) shifter_3 (.in(R1), .\dist (R2[4:0]), .out(shifter_3_out));
  Shifter #(.width(32), .shift("rr")) shifter_4 (.in(R1), .\dist (R2[4:0]), .out(shifter_4_out));
  assign bit_extender_1_out = {{31{1'b0}}, comparator_1_eq};  // Bit_Extender bit_extender_1
  assign bit_extender_2_out = {{31{1'b0}}, comparator_1_lt};  // Bit_Extender bit_extender_2
  not not_2 (not_2_out, subtractor_1_bout);
  Multiplexer #(.select(4), .width(32), .enable("false")) multiplexer_1 (
    .in0(xor_1_out), .in1(and_1_out), .in2(or_1_out), .in3(and_2_out), .in4(adder_1_out),
    .in5(bit_extender_1_out), .in6(subtractor_1_out), .in7(bit_extender_2_out), .in8(shifter_1_out),
    .in9(shifter_2_out), .in10(shifter_3_out), .in11(shifter_4_out), .in12({32{1'b0}}), .in13({32{1'b0}}),
    .in14({32{1'b0}}), .in15({32{1'b0}}), .out({N_flag, Result[30:0]}), .sel(opCode));
  Multiplexer #(.select(4), .enable("false")) multiplexer_2 (
    .in0(1'b0), .in1(1'b0), .in2(1'b0), .in3(1'b0), .in4(adder_1_cout), .in5(1'b0), .in6(not_2_out),
    .in7(1'b0), .in8(1'b0), .in9(1'b0), .in10(1'b0), .in11(1'b0), .in12(1'b0), .in13(1'b0), .in14(1'b0),
    .in15(1'b0), .out(c_flag), .sel(opCode));
  nor nor_1 (zero_flag, Result[0], Result[1], Result[2], Result[3], Result[4], Result[5], Result[6], Result[7], Result[8], Result[9], Result[10], Result[11], Result[12], Result[13], Result[14], Result[15], Result[16], Result[17], Result[18], Result[19], Result[20], Result[21], Result[22], Result[23], Result[24], Result[25], Result[26], Result[27], Result[28], Result[29], Result[30], N_flag);

  assign Result[31] = N_flag;

  // Other names for the same wires on the sheet: Reg1[31:0] = R1; Reg2[31:0] = R2
endmodule

module Datapath (
  input  pc_clear
);

  wire ALURes, clock_1_out, CMP, comparator_1_eq, comparator_1_lt, ExtOp, MemRead, MemWrite,
       multiplexer_3_out, RegDest, RegWrite, RegZX;
  wire [1:0] F, RegInput, Source2, updatePC;
  wire [2:0] alu_1_c_flag, Imm3, multiplexer_2_out, multiplexer_4_out;
  wire [3:0] opCode;
  wire [4:0] Op, shifter_2_out;
  wire [4:2] Imm5;
  wire [7:5] Imm11;
  wire [10:0] shifter_1_out;
  wire [19:0] adder_2_out, adder_3_out, bit_extender_2_out, bit_extender_3_out, bit_extender_7_out,
       multiplexer_6_out, multiplexer_7_out, newPC, PC, PC_2;
  wire [31:0] bit_extender_4_out, bit_extender_5_out, bit_extender_6_out, Imm3_Imm2, multiplexer_1_out,
       multiplexer_5_out, multiplexer_9_out, ram_1_data, Reg_y, RegZ;
  wire [31:1] alu_1_result;

  Register #(.width(20)) u_PC (.D(newPC), .en(1'b1), .Q(PC), .clk(clock_1_out), .clr(pc_clear));
  Clock clock_1 (.out(clock_1_out));
  assign Imm3_Imm2 = {{27{Imm3[2]}}, {Imm3, F}};  // Bit_Extender bit_extender_1
  Adder #(.width(20)) adder_1 (.a(PC), .b(20'h2), .out(PC_2), .cin(1'b0));  // open: cout
  ROM #(.addrWidth(20), .dataWidth(16)) rom_1 (.addr(PC), .data({Op, Imm3, Imm11, Imm5, F}));  // open: sel
  Control_Unit control_unit_1 (
    .OpCode(Op), .f(F), .MRead(MemRead), .MWrite(MemWrite), .Src2(Source2), .Ext_OP(ExtOp),
    .RWrite(RegWrite), .RDest(RegDest), .RInput(RegInput), .R_XZ(RegZX), .AluOperation(opCode),
    .PCSel(updatePC), .Comparator(CMP));
  Shifter #(.width(11)) shifter_1 (.in({Imm3, Imm11, Imm5, F}), .\dist (4'b0001), .out(shifter_1_out));
  Comparator #(.width(32)) comparator_1 (.a(RegZ), .b(Reg_y), .eq(comparator_1_eq), .lt(comparator_1_lt));  // open: gt
  assign bit_extender_2_out = {{9{shifter_1_out[10]}}, shifter_1_out};  // Bit_Extender bit_extender_2
  Shifter #(.width(5)) shifter_2 (.in({Imm5, F}), .\dist (3'b001), .out(shifter_2_out));
  Adder #(.width(20)) adder_2 (.a(PC), .b(bit_extender_2_out), .out(adder_2_out), .cin(1'b0));  // open: cout
  Multiplexer #(.select(2), .width(32), .enable("false")) multiplexer_1 (
    .in0(ram_1_data), .in1({alu_1_result, ALURes}), .in2(bit_extender_6_out), .out(multiplexer_1_out),
    .sel(RegInput));  // open: in3
  Multiplexer #(.width(3), .enable("false")) multiplexer_2 (
    .in0(Imm5), .in1(Imm3), .out(multiplexer_2_out), .sel(RegZX));
  assign bit_extender_3_out = {{15{shifter_2_out[4]}}, shifter_2_out};  // Bit_Extender bit_extender_3
  Multiplexer #(.enable("false")) multiplexer_3 (
    .in0(comparator_1_eq), .in1(comparator_1_lt), .out(multiplexer_3_out), .sel(CMP));
  Multiplexer #(.width(3), .enable("false")) multiplexer_4 (
    .in0(Imm3), .in1(3'b111), .out(multiplexer_4_out), .sel(RegDest));
  Adder #(.width(20)) adder_3 (.a(bit_extender_3_out), .b(PC), .out(adder_3_out), .cin(1'b0));  // open: cout
  RegFile regfile_1 (
    .S1(Imm11), .S2(multiplexer_2_out), .Rx(multiplexer_1_out), .RegDest(multiplexer_4_out), .WE(RegWrite),
    .Reg1(Reg_y), .Reg2(RegZ), .CLK(clock_1_out));
  assign bit_extender_4_out = {{27{1'b0}}, {Imm5, F}};  // Bit_Extender bit_extender_4
  Multiplexer #(.width(32), .enable("false")) multiplexer_5 (
    .in0(bit_extender_4_out), .in1(bit_extender_5_out), .out(multiplexer_5_out), .sel(ExtOp));
  assign bit_extender_5_out = {{27{Imm5[4]}}, {Imm5, F}};  // Bit_Extender bit_extender_5
  Multiplexer #(.width(20), .enable("false")) multiplexer_6 (
    .in0(PC_2), .in1(adder_3_out), .out(multiplexer_6_out), .sel(multiplexer_3_out));
  Multiplexer #(.width(20), .enable("false")) multiplexer_7 (
    .in0(adder_3_out), .in1(PC_2), .out(multiplexer_7_out), .sel(multiplexer_3_out));
  assign bit_extender_6_out = {{12{1'b0}}, PC_2};  // Bit_Extender bit_extender_6
  Multiplexer #(.select(2), .width(20), .enable("false")) multiplexer_8 (
    .in0(PC_2), .in1(multiplexer_6_out), .in2(multiplexer_7_out), .in3(adder_2_out), .out(newPC),
    .sel(updatePC));
  Multiplexer #(.select(2), .width(32), .enable("false")) multiplexer_9 (
    .in0(RegZ), .in1(multiplexer_5_out), .in2(Imm3_Imm2), .out(multiplexer_9_out), .sel(Source2));  // open: in3
  ALU alu_1 (
    .R1(Reg_y), .R2(multiplexer_9_out), .opCode(opCode), .Result({alu_1_result, ALURes}),
    .c_flag(alu_1_c_flag[0]), .zero_flag(alu_1_c_flag[1]), .N_flag(alu_1_c_flag[2]));
  Bit_Extender #(.in_width(32), .out_width(20)) bit_extender_7 (.in({alu_1_result, ALURes}), .out(bit_extender_7_out));
  Register #(.width(3)) NZC_Flags (.D(alu_1_c_flag), .clk(clock_1_out));  // open: en, Q, clr
  RAM #(.addrWidth(20), .dataWidth(32), .bus("separate")) ram_1 (
    .addr(bit_extender_7_out), .din(RegZ), .data(ram_1_data), .str(MemWrite), .clk(clock_1_out), .ld(MemRead));  // open: sel, clr

  // Other names for the same wires on the sheet: Ry[2:0] = Imm11; Imm11 (some bits) = {Imm3, Imm5, F}; Rx[2:0] = Imm3;
  //   Imm2[1:0] = F; Imm5[1:0] = F; Rz[2:0] = Imm5

  // Notes on the sheet:
  //   contents of rom_1 (hex, n*v repeats v):
  //   9160 0 9261 0 344 0 445 0 546 0 647 0 b44 0 b45 0 b46 0 b47 0 134f 0 1b4f 0 234f 0 2b4f 0 334f 0
  //   3b4f 0 434f 0 4b4f 0 5b82 0 63a1 0 6bc1 7*0 98e8 0 94e0 0 95e1 0 7586 0 8582 0 35bf 0 a001 0 349f 0
  //   a7fb
endmodule

// regwrit
module Control_Unit (
  input  [4:0] OpCode,
  input  [1:0] f,
  output MRead,
  output MWrite,
  output [1:0] Src2,
  output Ext_OP,
  output RWrite,
  output RDest,
  output [1:0] RInput,
  output R_XZ,
  output [3:0] AluOperation,
  output Comparator,
  output [1:0] PCSel
);

  ROM #(.addrWidth(5), .dataWidth(10)) rom_1 (
    .addr(OpCode), .data({R_XZ, RInput, RDest, RWrite, Ext_OP, Src2, MWrite, MRead}));  // open: sel
  ROM #(.addrWidth(7), .dataWidth(4)) rom_2 (.addr({OpCode, f}), .data(AluOperation));  // open: sel
  ROM #(.addrWidth(5), .dataWidth(3)) rom_3 (.addr(OpCode), .data({PCSel, Comparator}));  // open: sel

  // Notes on the sheet:
  //   contents of rom_1 (hex, n*v repeats v):
  //   a0 a0 4*a4 4*b4 4*a4 4*210 35 a 0 170
  //   contents of rom_2 (hex, n*v repeats v):
  //   1 3 2 0 4 6 5 7 4*1 4*3 4*2 4*0 4*4 4*6 4*5 4*7 4*e 4*9 4*8 4*b 8*5 8*7 8*4
  //   contents of rom_3 (hex, n*v repeats v):
  //   14*0 2 4 3 5 0 0 6 6
endmodule
